# Fritzing sketch LedSwitch (saved by Fritzing 0.9.3b)
breadboards: 1

parts:
  부품1 = Arduino Uno (Rev3)
  S1 = Pushbutton [package="[THT]"]
  LED1 = LED - 5mm [color="Red (633nm)" package="5 mm [THT]"]
  R1 = Resistor [tolerance=±5% resistance=220 package=THT]

nets:
  N1: 부품1.D8, R1.Pin_0
  N2: 부품1.GND, S1.Pin_1, S1.Pin_2, LED1.anode
  N3: 부품1.D2, 부품1.D3_PWM, S1.Pin_4
  N4: LED1.cathode, R1.Pin_1
